# Fritzing sketch Arduino VFD (saved by Fritzing 0.9.3b)

parts:
  J1 = male pin header, 4 pins [form="♂ (male)"]
  Part1 = Arduino Nano (Rev3.0)
  X1 = DB9 Connector [package=db9]
  JACK1 = 2.1mm Barrel Jack with Terminal Block
  J2 = male pin header, 3 pins [form="♂ (male)"]

nets:
  N1: J1.pin1, Part1.5V
  N2: J1.pin3, Part1.D9
  N3: J1.pin4, Part1.GND
  N4: X1.5, JACK1.NEG, J2.pin2
  N5: X1.8, J2.pin3
  N6: JACK1.POS, J2.pin1

notes:
  12V DC
  TTL RS232 Convertor
  AltSoftSerial library uses Pin 9 for transmit (Pin 8 is receive, but not required in this case, since we are only sending data *to* to t<module fritzingVersion="0.9.3b.04.19.5c895d327c44a3114e5fcc9d8260daf0cbb52806">
  <boundingRects>
  <boundingRect rect="0 0 0 0" name="PCB View"/>
  <boundingRect rect="4.66667 -62.5167 54 11.7" name="Breadboard View"/>
  <boundingRect rect="0 0 0 0" name="Schematic View"/>
  </boundingRects>
  <instances>
  <instance modelIndex="85577526" moduleIdRef="BreadboardLogoTextModuleID" path=":/resources/parts/core/breadboardlogotext.fzp">
  <property value="12V DC" name="logo"/>
  <property value="#787878" name="color"/>
  <property value="15.240000000000002" name="width"/>
  <property value="3.302" name="height"/>
  <property value="&lt;svg viewBox=&quot;0 0 60 13&quot; height=&quot;.13in&quot; xmlns=&quot;http://www.w3.org/2000/svg&quot; width=&quot;0.6in&quot;>&#xa; &lt;g id=&quot;breadboard&quot;>&#xa; &lt;text fill=&quot;#787878&quot; y=&quot;9&quot; x=&quot;30&quot; text-anchor=&quot;middle&quot; stroke-width=&quot;0&quot; id=&quot;label&quot; font-family=&quot;Droid Sans&quot; font-size=&quot;10&quot; xml:space=&quot;preserve&quot;>12V DC&lt;/text>&#xa; &lt;/g>&#xa;&lt;/svg>&#xa;" name="shape"/>
  <property value=":/resources/parts/svg/core/breadboard/breadboardlogo.svg" name="lastfilename"/>
  <title>TXT1</title>
  <views>
  <breadboardView layer="breadboard">
  <geometry z="2.50018" y="-62.5167" x="4.66667"/>
  </breadboardView>
  <schematicView layer="breadboard">
  <geometry z="0" y="222.15" x="554.667"/>
  </schematicView>
  <pcbView layer="">
  <geometry z="0" y="10" x="176.293"/>
  </pcbView>
  </views>
  </instance>
  </instances>
  </module>
  he display)
  MAX232 chip converts serial signals from TTL (0 - 5V) to RS232 (+15V - -15V). <module fritzingVersion="0.9.3b.04.19.5c895d327c44a3114e5fcc9d8260daf0cbb52806">
  <boundingRects>
  <boundingRect rect="0 0 0 0" name="PCB View"/>
  <boundingRect rect="169.333 -58 220 78" name="Breadboard View"/>
  <boundingRect rect="0 0 0 0" name="Schematic View"/>
  </boundingRects>
  <instances>
  <instance modelIndex="85577531" moduleIdRef="NoteModuleID" path=":/resources/parts/core/note.fzp">
  <title>Note1</title>
  <text>&lt;!DOCTYPE HTML PUBLIC "-//W3C//DTD HTML 4.0//EN" "http://www.w3.org/TR/REC-html40/strict.dtd">
  &lt;html>&lt;head>&lt;meta name="qrichtext" content="1" />&lt;style type="text/css">
  p, li { white-space: pre-wrap; }
  &lt;/style>&lt;/head>&lt;body style=" font-family:'Droid Sans'; font-size:9pt; font-weight:400; font-style:normal;">
  &lt;p style=" margin-top:0px; margin-bottom:0px; margin-left:0px; margin-right:0px; -qt-block-indent:0; text-indent:0px;">AltSoftSerial library uses Pin 9 for transmit (Pin 8 is receive, but not required in this case, since we are only sending data *to* to t&amp;lt;module fritzingVersion=&amp;quot;0.9.3b.04.19.5c895d327c44a3114e5fcc9d8260daf0cbb52806&amp;quot;&amp;gt;&lt;/p>
  &lt;p style=" margin-top:0px; margin-bottom:0px; margin-left:0px; margin-right:0px; -qt-block-indent:0; text-indent:0px;"> &amp;lt;boundingRects&amp;gt;&lt;/p>
  &lt;p style=" margin-top:0px; margin-bottom:0px; margin-left:0px; margin-right:0px; -qt-block-indent:0; text-indent:0px;"> &amp;lt;boundingRect rect=&amp;quot;0 0 0 0&amp;quot; name=&amp;quot;PCB View&amp;quot;/&amp;gt;&lt;/p>
  &lt;p style=" margin-top:0px; margin-bottom:0px; margin-left:0px; margin-right:0px; -qt-block-indent:0; text-indent:0px;"> &amp;lt;boundingRect rect=&amp;quot;4.66667 -62.5167 54 11.7&amp;quot; name=&amp;quot;Breadboard View&amp;quot;/&amp;gt;&lt;/p>
  &lt;p style=" margin-top:0px; margin-bottom:0px; margin-left:0px; margin-right:0px; -qt-block-indent:0; text-indent:0px;"> &amp;lt;boundingRect rect=&amp;quot;0 0 0 0&amp;quot; name=&amp;quot;Schematic View&amp;quot;/&amp;gt;&lt;/p>
  &lt;p style=" margin-top:0px; margin-bottom:0px; margin-left:0px; margin-right:0px; -qt-block-indent:0; text-indent:0px;"> &amp;lt;/boundingRects&amp;gt;&lt;/p>
  &lt;p style=" margin-top:0px; margin-bottom:0px; margin-left:0px; margin-right:0px; -qt-block-indent:0; text-indent:0px;"> &amp;lt;instances&amp;gt;&lt;/p>
  &lt;p style=" margin-top:0px; margin-bottom:0px; margin-left:0px; margin-right:0px; -qt-block-indent:0; text-indent:0px;"> &amp;lt;instance modelIndex=&amp;quot;85577526&amp;quot; moduleIdRef=&amp;quot;BreadboardLogoTextModuleID&amp;quot; path=&amp;quot;:/resources/parts/core/breadboardlogotext.fzp&amp;quot;&amp;gt;&lt;/p>
  &lt;p style=" margin-top:0px; margin-bottom:0px; margin-left:0px; margin-right:0px; -qt-block-indent:0; text-indent:0px;"> &amp;lt;property value=&amp;quot;12V DC&amp;quot; name=&amp;quot;logo&amp;quot;/&amp;gt;&lt;/p>
  &lt;p style=" margin-top:0px; margin-bottom:0px; margin-left:0px; margin-right:0px; -qt-block-indent:0; text-indent:0px;"> &amp;lt;property value=&amp;quot;#787878&amp;quot; name=&amp;quot;color&amp;quot;/&amp;gt;&lt;/p>
  &lt;p style=" margin-top:0px; margin-bottom:0px; margin-left:0px; margin-right:0px; -qt-block-indent:0; text-indent:0px;"> &amp;lt;property value=&amp;quot;15.240000000000002&amp;quot; name=&amp;quot;width&amp;quot;/&amp;gt;&lt;/p>
  &lt;p style=" margin-top:0px; margin-bottom:0px; margin-left:0px; margin-right:0px; -qt-block-indent:0; text-indent:0px;"> &amp;lt;property value=&amp;quot;3.302&amp;quot; name=&amp;quot;height&amp;quot;/&amp;gt;&lt;/p>
  &lt;p style=" margin-top:0px; margin-bottom:0px; margin-left:0px; margin-right:0px; -qt-block-indent:0; text-indent:0px;"> &amp;lt;property value=&amp;quot;&amp;amp;lt;svg viewBox=&amp;amp;quot;0 0 60 13&amp;amp;quot; height=&amp;amp;quot;.13in&amp;amp;quot; xmlns=&amp;amp;quot;http://www.w3.org/2000/svg&amp;amp;quot; width=&amp;amp;quot;0.6in&amp;amp;quot;&amp;gt;&amp;amp;#xa; &amp;amp;lt;g id=&amp;amp;quot;breadboard&amp;amp;quot;&amp;gt;&amp;amp;#xa; &amp;amp;lt;text fill=&amp;amp;quot;#787878&amp;amp;quot; y=&amp;amp;quot;9&amp;amp;quot; x=&amp;amp;quot;30&amp;amp;quot; text-anchor=&amp;amp;quot;middle&amp;amp;quot; stroke-width=&amp;amp;quot;0&amp;amp;quot; id=&amp;amp;quot;label&amp;amp;quot; font-family=&amp;amp;quot;Droid Sans&amp;amp;quot; font-size=&amp;amp;quot;10&amp;amp;quot; xml:space=&amp;amp;quot;preserve&amp;amp;quot;&amp;gt;12V DC&amp;amp;lt;/text&amp;gt;&amp;amp;#xa; &amp;amp;lt;/g&amp;gt;&amp;amp;#xa;&amp;amp;lt;/svg&amp;gt;&amp;amp;#xa;&amp;quot; name=&amp;quot;shape&amp;quot;/&amp;gt;&lt;/p>
  &lt;p style=" margin-top:0px; margin-bottom:0px; margin-left:0px; margin-right:0px; -qt-block-indent:0; text-indent:0px;"> &amp;lt;property value=&amp;quot;:/resources/parts/svg/core/breadboard/breadboardlogo.svg&amp;quot; name=&amp;quot;lastfilename&amp;quot;/&amp;gt;&lt;/p>
  &lt;p style=" margin-top:0px; margin-bottom:0px; margin-left:0px; margin-right:0px; -qt-block-indent:0; text-indent:0px;"> &amp;lt;title&amp;gt;TXT1&amp;lt;/title&amp;gt;&lt;/p>
  &lt;p style=" margin-top:0px; margin-bottom:0px; margin-left:0px; margin-right:0px; -qt-block-indent:0; text-indent:0px;"> &amp;lt;views&amp;gt;&lt;/p>
  &lt;p style=" margin-top:0px; margin-bottom:0px; margin-left:0px; margin-right:0px; -qt-block-indent:0; text-indent:0px;"> &amp;lt;breadboardView layer=&amp;quot;breadboard&amp;quot;&amp;gt;&lt;/p>
  &lt;p style=" margin-top:0px; margin-bottom:0px; margin-left:0px; margin-right:0px; -qt-block-indent:0; text-indent:0px;"> &amp;lt;geometry z=&amp;quot;2.50018&amp;quot; y=&amp;quot;-62.5167&amp;quot; x=&amp;quot;4.66667&amp;quot;/&amp;gt;&lt;/p>
  &lt;p style=" margin-top:0px; margin-bottom:0px; margin-left:0px; margin-right:0px; -qt-block-indent:0; text-indent:0px;"> &amp;lt;/breadboardView&amp;gt;&lt;/p>
  &lt;p style=" margin-top:0px; margin-bottom:0px; margin-left:0px; margin-right:0px; -qt-block-indent:0; text-indent:0px;"> &amp;lt;schematicView layer=&amp;quot;breadboard&amp;quot;&amp;gt;&lt;/p>
  &lt;p style=" margin-top:0px; margin-bottom:0px; margin-left:0px; margin-right:0px; -qt-block-indent:0; text-indent:0px;"> &amp;lt;geometry z=&amp;quot;0&amp;quot; y=&amp;quot;222.15&amp;quot; x=&amp;quot;554.667&amp;quot;/&amp;gt;&lt;/p>
  &lt;p style=" margin-top:0px; margin-bottom:0px; margin-left:0px; margin-right:0px; -qt-block-indent:0; text-indent:0px;"> &amp;lt;/schematicView&amp;gt;&lt;/p>
  &lt;p style=" margin-top:0px; margin-bottom:0px; margin-left:0px; margin-right:0px; -qt-block-indent:0; text-indent:0px;"> &amp;lt;pcbView layer=&amp;quot;&amp;quot;&amp;gt;&lt;/p>
  &lt;p style=" margin-top:0px; margin-bottom:0px; margin-left:0px; margin-right:0px; -qt-block-indent:0; text-indent:0px;"> &amp;lt;geometry z=&amp;quot;0&amp;quot; y=&amp;quot;10&amp;quot; x=&amp;quot;176.293&amp;quot;/&amp;gt;&lt;/p>
  &lt;p style=" margin-top:0px; margin-bottom:0px; margin-left:0px; margin-right:0px; -qt-block-indent:0; text-indent:0px;"> &amp;lt;/pcbView&amp;gt;&lt;/p>
  &lt;p style=" margin-top:0px; margin-bottom:0px; margin-left:0px; margin-right:0px; -qt-block-indent:0; text-indent:0px;"> &amp;lt;/views&amp;gt;&lt;/p>
  &lt;p style=" margin-top:0px; margin-bottom:0px; margin-left:0px; margin-right:0px; -qt-block-indent:0; text-indent:0px;"> &amp;lt;/instance&amp;gt;&lt;/p>
  &lt;p style=" margin-top:0px; margin-bottom:0px; margin-left:0px; margin-right:0px; -qt-block-indent:0; text-indent:0px;"> &amp;lt;/instances&amp;gt;&lt;/p>
  &lt;p style=" margin-top:0px; margin-bottom:0px; margin-left:0px; margin-right:0px; -qt-block-indent:0; text-indent:0px;">&amp;lt;/module&amp;gt;&lt;/p>
  &lt;p style=" margin-top:0px; margin-bottom:0px; margin-left:0px; margin-right:0px; -qt-block-indent:0; text-indent:0px;">he display)&lt;/p>&lt;/body>&lt;/html></text>
  <views>
  <breadboardView layer="breadboardNote">
  <geometry z="6.5" y="-58" x="169.333" height="78" width="220"/>
  </breadboardView>
  </views>
  </instance>
  </instances>
  </module>
  RS232 Pinout is Ground on Pin 5, Rx on Pin 2)
  VFD Display
